# Fritzing sketch Password_Keypad_MT1637 (saved by Fritzing 0.9.9b)
breadboards: 1

parts:
  Matrix_keypad1 = KEYPAD 4x4
  Part1 = Arduino Nano (Rev3.0)

nets:
  N1: Matrix_keypad1.col1, Part1.D5
  N2: Matrix_keypad1.col2, Part1.D4
  N3: Matrix_keypad1.col3, Part1.D3
  N4: Matrix_keypad1.col4, Part1.D2
  N5: Matrix_keypad1.row1, Part1.D6
  N6: Matrix_keypad1.row2, Part1.D7
  N7: Matrix_keypad1.row3, Part1.D8
  N8: Matrix_keypad1.row4, Part1.D9

custom parts:
  KEYPAD 4x4: Matrix keypad 16 buttons, 4 rows x 4 columns
